# Fritzing sketch uriel-sketch (saved by Fritzing 0.9.3b)
breadboards: 1

parts:
  Part1 = Arduino Uno (Rev3)
  12V_power_supply = Power plug
  RGB_led_strip = RGB LED - (4 legs) [package="5 mm [THT]"]
  10kΩ = Rotary Potentiometer (Small) [maximum_resistance=10kΩ package=THT]
  Potentiometers = Rotary Potentiometer (Small) [maximum_resistance=10kΩ package=THT]
  R6 = Rotary Potentiometer (Small) [maximum_resistance=10kΩ package=THT]
  S1 = Pushbutton [package="[SMD]"]
  NPN_2222A = TRANSISTOR_NPN [package=to-92-ammo]
  Q5 = TRANSISTOR_NPN [package=to-92-ammo]
  Q6 = TRANSISTOR_NPN [package=to-92-ammo]
  R10 = Resistor [tolerance=±5% resistance=10k package=THT]
  R11 = Resistor [tolerance=±5% resistance=10k package=THT]
  R12 = Resistor [tolerance=±5% resistance=10k package=THT]
  R13 = Resistor [tolerance=±5% resistance=10k package=THT]

nets:
  N1: Part1.A0, R6.wiper
  N2: Part1.A1, Potentiometers.wiper
  N3: Part1.A2, 10kΩ.wiper
  GND: Part1.GND, 12V_power_supply.GND, 10kΩ.leg1, Potentiometers.leg1, R6.leg1, S1.Pin_3, S1.Pin_4, NPN_2222A.E, Q5.E, Q6.E, R10.Pin_1, R11.Pin_1, R12.Pin_1
  N4: Part1.D3_PWM, Q5.B, R10.Pin_0
  N5: Part1.D5_PWM, NPN_2222A.B, R11.Pin_0
  N6: Part1.D6_PWM, Q6.B, R12.Pin_0
  N7: Part1.D7, S1.Pin_1, S1.Pin_2, R13.Pin_0
  N8: Part1.5V, 10kΩ.leg2, Potentiometers.leg2, R6.leg2, R13.Pin_1
  N9: 12V_power_supply.VCC, RGB_led_strip.common_anode
  N10: RGB_led_strip.red_cathode, Q5.C
  N11: RGB_led_strip.green_cathode, NPN_2222A.C
  N12: RGB_led_strip.blue_cathode, Q6.C
